# Fritzing sketch tft144 (saved by Fritzing 0.9.3b)
breadboards: 1

parts:
  Part2 = Arduino Nano (Rev3.0)
  Part3 = Adafruit 1.44 inch TFT Breakout [part_number="Adafruit #2088"]

nets:
  GND: Part2.GND, Part3.GND
  N1: Part2.D8, Part3.TFTDC
  N2: Part2.D9, Part3.RESET
  N3: Part2.D10, Part3.TFTCS
  N4: Part2.D11/MOSI, Part3.MOSI
  N5: Part2.D12/MISO, Part3.MISO
  3V3: Part2.3V3, Part3.VIN
  N6: Part2.D13/SCK, Part3.SCK

custom parts:
  Adafruit 1.44 inch TFT Breakout: This lovely little display breakout is the best way to add a small, colorful and bright display to any project. Since the display uses 4-wire SPI to communicate and has its own pixel-addressable frame buffer, it can be used with every kind of microcontroller. Even a very small one with low memory and few pins available! The 1.44" display has 128x128 color pixels. Unlike the low cost "Nokia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
